// Digital circuit alu.dig as structural Verilog
module alu (
  input  [31:0] A,
  input  [31:0] B,
  input  [3:0] ALUControl,
  output Zero,
  output [31:0] Result
);

  wire comparator_1_lt, comparator_2_lt;
  wire [31:0] add_1_s, and_1_out, barrelshifter_1_out, barrelshifter_2_out, barrelshifter_3_out, div_1_q,
       div_1_r, multiplexer_1_out, multiplexer_2_out, or_1_out, sub_1_s, xor_1_out;
  wire [63:0] mul_1_mul;

  assign and_1_out = A & B;  // And and_1, 32 bits wide
  assign or_1_out = A | B;  // Or or_1, 32 bits wide
  Add #(.Bits(32)) add_1 (.a(A), .b(B), .c_i(1'b0), .s(add_1_s));  // open: c_o
  Sub #(.Bits(32)) sub_1 (.a(A), .b(B), .c_i(1'b0), .s(sub_1_s));  // open: c_o
  Comparator #(.Signed("true"), .Bits(32)) comparator_1 (.a(A), .b(B), .lt(comparator_1_lt));  // open: gt, eq
  assign xor_1_out = A ^ B;  // XOr xor_1, 32 bits wide
  Comparator #(.Bits(32)) comparator_2 (.a(A), .b(B), .lt(comparator_2_lt));  // open: gt, eq
  BarrelShifter #(.Bits(32)) barrelshifter_1 (.in(A), .shift(B[5:0]), .out(barrelshifter_1_out));
  BarrelShifter #(.Bits(32), .direction("right")) barrelshifter_2 (.in(A), .shift(B[5:0]), .out(barrelshifter_2_out));
  BarrelShifter #(.Bits(32), .barrelShifterMode("arithmetic"), .barrelSigned("true"), .direction("right")) barrelshifter_3 (
    .in(A), .shift(B[6:0]), .out(barrelshifter_3_out));
  Mul #(.Bits(32)) mul_1 (.a(A), .b(B), .mul(mul_1_mul));
  Div #(.Bits(32)) div_1 (.a(A), .b(B), .q(div_1_q), .r(div_1_r));
  Multiplexer #(.Bits(32)) multiplexer_1 (
    .sel(comparator_1_lt), .in_0({32{1'b0}}), .in_1(32'h1), .out(multiplexer_1_out));
  Multiplexer #(.Bits(32)) multiplexer_2 (
    .sel(comparator_2_lt), .in_0({32{1'b0}}), .in_1(32'h1), .out(multiplexer_2_out));
  Multiplexer #(.Selector_Bits(4), .Bits(32)) multiplexer_3 (
    .sel(ALUControl), .in_0(and_1_out), .in_1(or_1_out), .in_2(add_1_s), .in_3(xor_1_out),
    .in_4(barrelshifter_1_out), .in_5(barrelshifter_2_out), .in_6(sub_1_s), .in_7(multiplexer_1_out),
    .in_8(multiplexer_2_out), .in_9(mul_1_mul[31:0]), .in_10(div_1_q), .in_11(div_1_r), .in_12({32{1'b0}}),
    .in_13(barrelshifter_3_out), .in_14({32{1'b0}}), .in_15({32{1'b0}}), .out(Result));
  Comparator #(.Signed("true"), .Bits(32)) comparator_3 (.a(Result), .b({32{1'b0}}), .eq(Zero));  // open: gt, lt
endmodule
