// Digital circuit aluControl.dig as structural Verilog
module aluControl (
  input  [2:0] funct3,
  input  [6:0] funct7,
  input  [1:0] ALUOp,
  input  I,
  output [3:0] ALUControl
);

  wire comparator_1_eq, comparator_2_eq, comparator_3_eq, comparator_4_eq, comparator_5_eq;
  wire [3:0] multiplexer_3_out, multiplexer_4_out, multiplexer_5_out, multiplexer_6_out, multiplexer_8_out,
       multiplexer_9_out, multiplexer_10_out;
  wire [6:0] multiplexer_1_out, multiplexer_2_out, multiplexer_7_out;

  Multiplexer #(.Bits(7)) multiplexer_1 (.sel(I), .in_0(funct7), .in_1({7{1'b0}}), .out(multiplexer_1_out));
  Comparator #(.Bits(10)) comparator_1 (.a({funct7, funct3}), .b(10'h100), .eq(comparator_1_eq));  // open: gt, lt
  Comparator #(.Bits(7)) comparator_2 (.a(funct7), .b(7'b0000001), .eq(comparator_2_eq));  // open: gt, lt
  Multiplexer #(.Bits(7)) multiplexer_2 (
    .sel(funct7[0]), .in_0({7{1'b0}}), .in_1(multiplexer_1_out), .out(multiplexer_2_out));
  Multiplexer #(.Bits(4)) multiplexer_3 (
    .sel(comparator_1_eq), .in_0(4'b0010), .in_1(4'b0110), .out(multiplexer_3_out));
  Comparator #(.Bits(10)) comparator_3 (.a({funct7, funct3}), .b(10'h105), .eq(comparator_3_eq));  // open: gt, lt
  Comparator #(.Bits(3)) comparator_4 (.a(funct3), .b(3'b101), .eq(comparator_4_eq));  // open: gt, lt
  Multiplexer #(.Bits(4)) multiplexer_4 (
    .sel(comparator_3_eq), .in_0(multiplexer_3_out), .in_1(4'b1101), .out(multiplexer_4_out));
  Multiplexer #(.Selector_Bits(3), .Bits(4)) multiplexer_5 (
    .sel(funct3), .in_0(4'b1001), .in_1(4'b0000), .in_2(4'b0000), .in_3(4'b0000), .in_4(4'b1010),
    .in_5(4'b0000), .in_6(4'b1011), .in_7(4'b0000), .out(multiplexer_5_out));
  Multiplexer #(.Bits(4)) multiplexer_6 (
    .sel(comparator_2_eq), .in_0(multiplexer_4_out), .in_1(multiplexer_5_out), .out(multiplexer_6_out));
  Multiplexer #(.Bits(7)) multiplexer_7 (
    .sel(comparator_4_eq), .in_0(multiplexer_2_out), .in_1(funct7), .out(multiplexer_7_out));
  Comparator #(.Bits(7)) comparator_5 (.a(multiplexer_7_out), .b({7{1'b0}}), .eq(comparator_5_eq));  // open: gt, lt
  Multiplexer #(.Selector_Bits(3), .Bits(4)) multiplexer_8 (
    .sel(funct3), .in_0(4'b0110), .in_1(4'b0110), .in_2(4'b1111), .in_3(4'b1111), .in_4(4'b0111),
    .in_5(4'b0111), .in_6(4'b1000), .in_7(4'b1000), .out(multiplexer_8_out));
  Multiplexer #(.Selector_Bits(3), .Bits(4)) multiplexer_9 (
    .sel(funct3), .in_0(4'b0010), .in_1(4'b0100), .in_2(4'b0111), .in_3(4'b1000), .in_4(4'b0011),
    .in_5(4'b0101), .in_6(4'b0001), .in_7(4'b0000), .out(multiplexer_9_out));
  Multiplexer #(.Bits(4)) multiplexer_10 (
    .sel(comparator_5_eq), .in_0(multiplexer_6_out), .in_1(multiplexer_9_out), .out(multiplexer_10_out));
  Multiplexer #(.Selector_Bits(2), .Bits(4)) multiplexer_11 (
    .sel(ALUOp), .in_0(4'b0010), .in_1(multiplexer_8_out), .in_2(multiplexer_10_out), .in_3(4'b1111),
    .out(ALUControl));

  // Notes on the sheet:
  //   Newly Added
  //   Branch
  //   R and I
endmodule
