// Digital circuit controlUnit.dig as structural Verilog
module controlUnit (
  input  [6:0] opcode,
  output Branch,
  output MemRead,
  output MemtoReg,
  output [1:0] ALUOp,
  output MemWrite,
  output ALUSrc,
  output RegWrite,
  output Jal,
  output Jalr,
  output LUI,
  output AUIPC,
  output I,
  output R
);

  wire not_1_out, not_2_out, not_3_out, not_4_out, not_5_out, not_6_out, not_7_out;
  wire [1:0] multiplexer_1_out;
  wire [2:0] or_2_out;

  not not_1 (not_1_out, opcode[6]);
  not not_2 (not_2_out, opcode[5]);
  not not_3 (not_3_out, opcode[4]);
  not not_4 (not_4_out, opcode[3]);
  not not_5 (not_5_out, opcode[2]);
  not not_6 (not_6_out, opcode[1]);
  not not_7 (not_7_out, opcode[0]);
  and and_1 (MemRead, opcode[0], opcode[1], not_5_out, not_4_out, not_3_out, not_2_out, not_1_out);
  and and_2 (MemWrite, opcode[0], opcode[1], not_5_out, not_4_out, not_3_out, opcode[5], not_1_out);
  and and_3 (Branch, opcode[0], opcode[1], not_5_out, not_4_out, not_3_out, opcode[5], opcode[6]);
  and and_4 (I, opcode[0], opcode[1], not_5_out, not_4_out, opcode[4], not_2_out, not_1_out);
  and and_5 (R, opcode[0], opcode[1], not_5_out, not_4_out, opcode[4], opcode[5], not_1_out);
  and and_6 (Jal, opcode[0], opcode[1], opcode[2], opcode[3], not_3_out, opcode[5], opcode[6]);
  and and_7 (Jalr, opcode[0], opcode[1], opcode[2], not_4_out, not_3_out, opcode[5], opcode[6]);
  and and_8 (LUI, not_1_out, opcode[5], opcode[4], not_4_out, opcode[2], opcode[1], opcode[0]);
  and and_9 (AUIPC, not_1_out, not_2_out, opcode[4], not_4_out, opcode[2], opcode[1], opcode[0]);
  or or_1 (ALUSrc, MemRead, MemWrite, I, Jalr);
  nor nor_1 (RegWrite, MemWrite, Branch);
  or or_2 (or_2_out[2], I, Branch, MemWrite, MemRead);
  or or_3 (or_2_out[1], Jal, R, MemWrite, MemRead);
  or or_4 (or_2_out[0], Jalr, R, Branch, MemRead);
  Multiplexer #(.Selector_Bits(3), .Bits(2)) multiplexer_1 (
    .sel(or_2_out), .in_0(2'b00), .in_1(2'b00), .in_2(2'b00), .in_3(2'b10), .in_4(2'b10), .in_5(2'b01),
    .in_6(2'b00), .in_7(2'b00), .out(multiplexer_1_out));
  Multiplexer #(.Selector_Bits(2), .Bits(2)) multiplexer_2 (
    .sel({AUIPC, LUI}), .in_0(multiplexer_1_out), .in_1(2'b11), .in_2(2'b00), .in_3(2'b00), .out(ALUOp));

  assign MemtoReg = MemRead;

  // Other names for the same wires on the sheet: B = Branch; L = MemRead; S = MemWrite

  // Notes on the sheet:
  //   0000011
  //   0100011
  //   1100011
  //   0010011
  //   0110011
  //   1101111
  //   1100111
  //   0110111
  //   0010111
endmodule
