// Digital circuit signExtend.dig as structural Verilog
module signExtend (
  input  [31:0] instr,
  input  [6:0] opcode,
  output [31:0] imm
);

  wire AUIPC, B, I, JAL, JALR, L, LUI, not_1_out, not_2_out, not_3_out, not_4_out, not_5_out, not_6_out,
       not_7_out, R, S;
  wire [2:0] multiplexer_1_out, or_1_out;
  wire [10:0] bitextender_3_out;
  wire [18:0] bitextender_2_out;
  wire [19:0] bitextender_1_out;

  not not_1 (not_1_out, opcode[6]);
  not not_2 (not_2_out, opcode[5]);
  not not_3 (not_3_out, opcode[4]);
  not not_4 (not_4_out, opcode[3]);
  not not_5 (not_5_out, opcode[2]);
  not not_6 (not_6_out, opcode[1]);
  not not_7 (not_7_out, opcode[0]);
  and and_1 (L, opcode[0], opcode[1], not_5_out, not_4_out, not_3_out, not_2_out, not_1_out);
  and and_2 (S, opcode[0], opcode[1], not_5_out, not_4_out, not_3_out, opcode[5], not_1_out);
  and and_3 (B, opcode[0], opcode[1], not_5_out, not_4_out, not_3_out, opcode[5], opcode[6]);
  and and_4 (I, opcode[0], opcode[1], not_5_out, not_4_out, opcode[4], not_2_out, not_1_out);
  and and_5 (R, opcode[0], opcode[1], not_5_out, not_4_out, opcode[4], opcode[5], not_1_out);
  and and_6 (JAL, opcode[0], opcode[1], opcode[2], opcode[3], not_3_out, opcode[5], opcode[6]);
  and and_7 (JALR, opcode[0], opcode[1], opcode[2], not_4_out, not_3_out, opcode[5], opcode[6]);
  and and_8 (LUI, not_1_out, opcode[5], opcode[4], not_4_out, opcode[2], opcode[1], opcode[0]);
  and and_9 (AUIPC, not_1_out, not_2_out, opcode[4], not_4_out, opcode[2], opcode[1], opcode[0]);
  BitExtender #(.inputBits(1), .outputBits(20)) bitextender_1 (.in(instr[31]), .out(bitextender_1_out));
  BitExtender #(.inputBits(1), .outputBits(19)) bitextender_2 (.in(instr[31]), .out(bitextender_2_out));
  BitExtender #(.inputBits(1), .outputBits(11)) bitextender_3 (.in(instr[31]), .out(bitextender_3_out));
  or or_1 (or_1_out[2], I, B, S, L);
  or or_2 (or_1_out[1], JAL, R, S, L);
  or or_3 (or_1_out[0], JALR, R, B, L);
  Multiplexer #(.Selector_Bits(2), .Bits(3)) multiplexer_1 (
    .sel({AUIPC, LUI}), .in_0(or_1_out), .in_1(3'b011), .in_2(3'b000), .in_3(3'b000), .out(multiplexer_1_out));
  Multiplexer #(.Selector_Bits(3), .Bits(32)) multiplexer_2 (
    .sel(multiplexer_1_out), .in_0({instr[31:12], {12{1'b0}}}), .in_1({bitextender_1_out, instr[31:20]}),
    .in_2({bitextender_3_out, instr[31], instr[19:12], instr[20], instr[30:21], 1'b0}),
    .in_3({instr[31:12], {12{1'b0}}}), .in_4({bitextender_1_out, instr[31:20]}),
    .in_5({bitextender_2_out, instr[31], instr[7], instr[30:25], instr[11:8], 1'b0}),
    .in_6({bitextender_1_out, instr[31:25], instr[11:7]}), .in_7({bitextender_1_out, instr[31:20]}), .out(imm));

  // Other names for the same wires on the sheet: LUI_AUIPC_sel[1:0] = {AUIPC, LUI}

  // Notes on the sheet:
  //   0000011
  //   0100011
  //   1100011
  //   0010011
  //   0110011
  //   1101111
  //   1100111
  //   0110111
  //   0010111
endmodule
