// Digital circuit testDisplay.dig as structural Verilog
module testDisplay (
  input  [3:0] ALUControl,
  input  [2:0] funct3,
  input  [6:0] funct7,
  input  [6:0] opcode,
  output [15:0] D1,
  output P1,
  output P2,
  output P3,
  output P4,
  output P5,
  output P6,
  output [15:0] D2,
  output [15:0] D3,
  output [15:0] D4,
  output [15:0] D5,
  output [15:0] D6
);

  wire and_10_out, and_11_out, and_12_out, and_13_out, AUIPC, B, comparator_1_eq, comparator_2_eq,
       comparator_3_eq, comparator_4_eq, comparator_5_eq, comparator_6_eq, I, JAL, JALR, L, LUI, not_1_out,
       not_2_out, not_3_out, not_4_out, not_5_out, not_6_out, not_7_out, R, S;
  wire [2:0] multiplexer_3_out, multiplexer_11_out, or_1_out;
  wire [6:0] multiplexer_1_out, multiplexer_4_out, multiplexer_6_out, multiplexer_8_out, multiplexer_9_out,
       multiplexer_10_out, multiplexer_12_out, multiplexer_13_out, multiplexer_14_out, multiplexer_15_out,
       multiplexer_16_out, multiplexer_17_out, multiplexer_18_out, multiplexer_19_out, multiplexer_20_out,
       multiplexer_21_out, multiplexer_22_out, multiplexer_23_out, multiplexer_24_out, multiplexer_25_out,
       multiplexer_26_out, multiplexer_27_out, multiplexer_29_out, multiplexer_30_out, multiplexer_31_out,
       multiplexer_32_out, multiplexer_33_out, multiplexer_34_out, multiplexer_35_out, multiplexer_36_out,
       multiplexer_37_out, multiplexer_38_out, multiplexer_39_out, multiplexer_40_out, multiplexer_42_out,
       multiplexer_44_out, temp1, w0, w1, w2, y0, y1, y2;

  not not_1 (not_1_out, opcode[6]);
  not not_2 (not_2_out, opcode[5]);
  not not_3 (not_3_out, opcode[4]);
  not not_4 (not_4_out, opcode[3]);
  not not_5 (not_5_out, opcode[2]);
  not not_6 (not_6_out, opcode[1]);
  not not_7 (not_7_out, opcode[0]);
  and and_1 (L, opcode[0], opcode[1], not_5_out, not_4_out, not_3_out, not_2_out, not_1_out);
  and and_2 (S, opcode[0], opcode[1], not_5_out, not_4_out, not_3_out, opcode[5], not_1_out);
  and and_3 (B, opcode[0], opcode[1], not_5_out, not_4_out, not_3_out, opcode[5], opcode[6]);
  and and_4 (I, opcode[0], opcode[1], not_5_out, not_4_out, opcode[4], not_2_out, not_1_out);
  and and_5 (R, opcode[0], opcode[1], not_5_out, not_4_out, opcode[4], opcode[5], not_1_out);
  and and_6 (JAL, opcode[0], opcode[1], opcode[2], opcode[3], not_3_out, opcode[5], opcode[6]);
  and and_7 (JALR, opcode[0], opcode[1], opcode[2], not_4_out, not_3_out, opcode[5], opcode[6]);
  and and_8 (LUI, not_1_out, opcode[5], opcode[4], not_4_out, opcode[2], opcode[1], opcode[0]);
  and and_9 (AUIPC, not_1_out, not_2_out, opcode[4], not_4_out, opcode[2], opcode[1], opcode[0]);
  Comparator #(.Bits(10)) comparator_1 (.a({funct7, funct3}), .b(10'h100), .eq(comparator_1_eq));  // open: gt, lt
  Comparator #(.Bits(10)) comparator_2 (.a({funct7, funct3}), .b(10'h105), .eq(comparator_2_eq));  // open: gt, lt
  or or_1 (or_1_out[2], I, B, S, L);
  or or_2 (or_1_out[1], JAL, R, S, L);
  or or_3 (or_1_out[0], JALR, R, B, L);
  and and_10 (and_10_out, ~comparator_2_eq, ALUControl[3]);  // And
  Multiplexer #(.Bits(7)) multiplexer_1 (
    .sel(ALUControl[3]), .in_0(7'b1000001), .in_1(7'b1001100), .out(multiplexer_1_out));
  Multiplexer #(.Bits(7)) multiplexer_2 (.sel(comparator_1_eq), .in_0(7'b0100000), .in_1(7'b1010011), .out(w0));
  Multiplexer #(.Selector_Bits(2), .Bits(3)) multiplexer_3 (
    .sel({AUIPC, LUI}), .in_0(or_1_out), .in_1(3'b000), .in_2(3'b000), .in_3(3'b000), .out(multiplexer_3_out));
  Multiplexer #(.Bits(7)) multiplexer_4 (
    .sel(ALUControl[3]), .in_0(7'b1001110), .in_1(7'b1010100), .out(multiplexer_4_out));
  Multiplexer #(.Bits(7)) multiplexer_5 (.sel(comparator_1_eq), .in_0(7'b0100000), .in_1(7'b1010101), .out(w1));
  Multiplexer #(.Bits(7)) multiplexer_6 (
    .sel(ALUControl[3]), .in_0(7'b1000100), .in_1(7'b1001001), .out(multiplexer_6_out));
  Multiplexer #(.Bits(7)) multiplexer_7 (.sel(comparator_1_eq), .in_0(7'b0100000), .in_1(7'b1000010), .out(w2));
  Multiplexer #(.Bits(7)) multiplexer_8 (
    .sel(and_10_out), .in_0(7'b0100000), .in_1(7'b1010011), .out(multiplexer_8_out));
  Multiplexer #(.Selector_Bits(3), .Bits(7)) multiplexer_9 (
    .sel(ALUControl[2:0]), .in_0(multiplexer_1_out), .in_1(7'b0100000), .in_2(7'b1000001), .in_3(7'b1011000),
    .in_4(7'b1010011), .in_5(7'b1010011), .in_6(7'b0100000), .in_7(7'b1010011), .out(multiplexer_9_out));
  Multiplexer #(.Bits(7)) multiplexer_10 (
    .sel(ALUControl[3]), .in_0(7'b1001001), .in_1(7'b1010101), .out(multiplexer_10_out));
  Comparator #(.Bits(4)) comparator_3 (.a(ALUControl), .b(4'b1101), .eq(comparator_3_eq));  // open: gt, lt
  Multiplexer #(.Bits(3)) multiplexer_11 (
    .sel(comparator_3_eq), .in_0(ALUControl[2:0]), .in_1(3'b110), .out(multiplexer_11_out));
  Multiplexer #(.Selector_Bits(3), .Bits(7)) multiplexer_12 (
    .sel(ALUControl[2:0]), .in_0(multiplexer_4_out), .in_1(7'b1001111), .in_2(7'b1000100), .in_3(7'b1001111),
    .in_4(7'b1001100), .in_5(7'b1010010), .in_6(7'b0100000), .in_7(7'b1001100), .out(multiplexer_12_out));
  Multiplexer #(.Selector_Bits(3), .Bits(7)) multiplexer_13 (
    .sel(multiplexer_11_out), .in_0(multiplexer_6_out), .in_1(7'b1010010), .in_2(7'b1000100),
    .in_3(7'b1010010), .in_4(7'b1001100), .in_5(7'b1001100), .in_6(7'b1000001), .in_7(7'b1010100),
    .out(multiplexer_13_out));
  Comparator #(.Bits(4)) comparator_4 (.a(ALUControl), .b(4'b1001), .eq(comparator_4_eq));  // open: gt, lt
  Comparator #(.Bits(3)) comparator_5 (.a(funct3), .b(3'b000), .eq(comparator_5_eq));  // open: gt, lt
  Multiplexer #(.Selector_Bits(3), .Bits(7)) multiplexer_14 (
    .sel(multiplexer_3_out), .in_0(7'b0100000), .in_1(7'b0100000), .in_2(7'b0100000), .in_3(7'b0100000),
    .in_4(7'b0100000), .in_5(7'b0100000), .in_6(7'b0100000), .in_7(7'b0100000), .out(multiplexer_14_out));
  Multiplexer #(.Selector_Bits(3), .Bits(7)) multiplexer_15 (
    .sel(funct3), .in_0(7'b1000010), .in_1(7'b1000010), .in_2(7'b1000001), .in_3(7'b0100000),
    .in_4(7'b1000010), .in_5(7'b1000010), .in_6(7'b1001100), .in_7(7'b1000111), .out(multiplexer_15_out));
  Multiplexer #(.Selector_Bits(3), .Bits(7)) multiplexer_16 (
    .sel(funct3), .in_0(7'b0100000), .in_1(7'b0100000), .in_2(7'b0100000), .in_3(7'b0100000),
    .in_4(7'b0100000), .in_5(7'b0100000), .in_6(7'b1000010), .in_7(7'b1000010), .out(multiplexer_16_out));
  and and_11 (and_11_out, comparator_4_eq, comparator_5_eq);
  ROM #(.AddrBits(7), .Bits(16)) ASCII (.A(multiplexer_14_out), .sel(1'b1), .D(D1));
  Multiplexer #(.Selector_Bits(2), .Bits(7)) multiplexer_17 (
    .sel({AUIPC, LUI}), .in_0(7'b0100000), .in_1(7'b0100000), .in_2(7'b1000001), .in_3(7'b0100000),
    .out(multiplexer_17_out));
  Multiplexer #(.Selector_Bits(3), .Bits(7)) multiplexer_18 (
    .sel(ALUControl[2:0]), .in_0(multiplexer_10_out), .in_1(7'b1001001), .in_2(7'b1001001),
    .in_3(7'b1001001), .in_4(7'b1001001), .in_5(7'b1001001), .in_6(7'b0100000), .in_7(7'b1001001),
    .out(multiplexer_18_out));
  Multiplexer #(.Selector_Bits(3), .Bits(7)) multiplexer_19 (
    .sel(multiplexer_3_out), .in_0(multiplexer_17_out), .in_1(7'b0100000), .in_2(7'b0100000),
    .in_3(7'b0100000), .in_4(multiplexer_8_out), .in_5(7'b0100000), .in_6(7'b0100000), .in_7(7'b0100000),
    .out(multiplexer_19_out));
  Multiplexer #(.Selector_Bits(3), .Bits(7)) multiplexer_20 (
    .sel(funct3), .in_0(7'b1000101), .in_1(7'b1001110), .in_2(7'b1000100), .in_3(7'b0100000),
    .in_4(7'b1001100), .in_5(7'b1000111), .in_6(7'b1010100), .in_7(7'b1000101), .out(multiplexer_20_out));
  Multiplexer #(.Bits(7)) multiplexer_21 (.sel(and_11_out), .in_0(temp1), .in_1(7'b1001101), .out(multiplexer_21_out));
  ROM #(.AddrBits(7), .Bits(16)) ASCII_2 (.A(multiplexer_19_out), .sel(1'b1), .D(D2));
  Multiplexer #(.Selector_Bits(2), .Bits(7)) multiplexer_22 (
    .sel({AUIPC, LUI}), .in_0(7'b0100000), .in_1(7'b0100000), .in_2(7'b1010101), .in_3(7'b0100000),
    .out(multiplexer_22_out));
  Multiplexer #(.Bits(7)) multiplexer_23 (
    .sel(and_12_out), .in_0(7'b0100000), .in_1(7'b1010011), .out(multiplexer_23_out));
  Multiplexer #(.Selector_Bits(3), .Bits(7)) multiplexer_24 (
    .sel(funct3), .in_0(7'b1010001), .in_1(7'b1000101), .in_2(7'b1000100), .in_3(7'b0100000),
    .in_4(7'b1010100), .in_5(7'b1010100), .in_6(7'b1010101), .in_7(7'b1010101), .out(multiplexer_24_out));
  Multiplexer #(.Selector_Bits(3), .Bits(7)) multiplexer_25 (
    .sel(multiplexer_3_out), .in_0(multiplexer_22_out), .in_1(7'b1001010), .in_2(7'b0100000),
    .in_3(multiplexer_23_out), .in_4(multiplexer_9_out), .in_5(multiplexer_16_out), .in_6(7'b0100000),
    .in_7(7'b0100000), .out(multiplexer_25_out));
  and and_12 (and_12_out, and_13_out, ~and_11_out);  // And
  and and_13 (and_13_out, ALUControl[3], ~comparator_2_eq);  // And
  ROM #(.AddrBits(7), .Bits(16)) ASCII_3 (.A(multiplexer_25_out), .sel(1'b1), .D(D3));
  Multiplexer #(.Selector_Bits(2), .Bits(7)) multiplexer_26 (
    .sel({AUIPC, LUI}), .in_0(7'b0100000), .in_1(7'b1001100), .in_2(7'b1001001), .in_3(7'b0100000),
    .out(multiplexer_26_out));
  Multiplexer #(.Selector_Bits(3), .Bits(7)) multiplexer_27 (
    .sel(ALUControl[2:0]), .in_0(y0), .in_1(7'b0100000), .in_2(7'b1000001), .in_3(7'b1011000),
    .in_4(7'b1010011), .in_5(7'b1010011), .in_6(w0), .in_7(7'b1010011), .out(multiplexer_27_out));
  Multiplexer #(.Bits(7)) multiplexer_28 (
    .sel(comparator_2_eq), .in_0(multiplexer_27_out), .in_1(7'b1010011), .out(temp1));
  Multiplexer #(.Selector_Bits(3), .Bits(7)) multiplexer_29 (
    .sel(multiplexer_3_out), .in_0(multiplexer_26_out), .in_1(7'b1000001), .in_2(7'b1001010),
    .in_3(multiplexer_21_out), .in_4(multiplexer_12_out), .in_5(multiplexer_15_out), .in_6(7'b0100000),
    .in_7(7'b0100000), .out(multiplexer_29_out));
  Multiplexer #(.Selector_Bits(3), .Bits(7)) multiplexer_30 (
    .sel(ALUControl[2:0]), .in_0(y1), .in_1(7'b1001111), .in_2(7'b1000100), .in_3(7'b1001111),
    .in_4(7'b1001100), .in_5(7'b1010010), .in_6(w1), .in_7(7'b1001100), .out(multiplexer_30_out));
  Multiplexer #(.Bits(7)) multiplexer_31 (
    .sel(comparator_2_eq), .in_0(multiplexer_30_out), .in_1(7'b1010010), .out(multiplexer_31_out));
  ROM #(.AddrBits(7), .Bits(16)) ASCII_4 (.A(multiplexer_29_out), .sel(1'b1), .D(D4));
  Multiplexer #(.Selector_Bits(2), .Bits(7)) multiplexer_32 (
    .sel({AUIPC, LUI}), .in_0(7'b0100000), .in_1(7'b1010101), .in_2(7'b1010000), .in_3(7'b0100000),
    .out(multiplexer_32_out));
  Multiplexer #(.Bits(7)) multiplexer_33 (
    .sel(and_11_out), .in_0(multiplexer_31_out), .in_1(7'b1010101), .out(multiplexer_33_out));
  Multiplexer #(.Selector_Bits(3), .Bits(7)) multiplexer_34 (
    .sel(multiplexer_3_out), .in_0(multiplexer_32_out), .in_1(7'b1001100), .in_2(7'b1000001),
    .in_3(multiplexer_33_out), .in_4(multiplexer_13_out), .in_5(multiplexer_20_out), .in_6(7'b1010011),
    .in_7(7'b1001100), .out(multiplexer_34_out));
  Multiplexer #(.Selector_Bits(3), .Bits(7)) multiplexer_35 (
    .sel(ALUControl[2:0]), .in_0(y2), .in_1(7'b1010010), .in_2(7'b1000100), .in_3(7'b1010010),
    .in_4(7'b1001100), .in_5(7'b1001100), .in_6(w2), .in_7(7'b1010100), .out(multiplexer_35_out));
  ROM #(.AddrBits(7), .Bits(16)) ASCII_5 (.A(multiplexer_34_out), .sel(1'b1), .D(D5));
  Multiplexer #(.Selector_Bits(2), .Bits(7)) multiplexer_36 (
    .sel({AUIPC, LUI}), .in_0(7'b0100000), .in_1(7'b1001001), .in_2(7'b1000011), .in_3(7'b0100000),
    .out(multiplexer_36_out));
  Multiplexer #(.Bits(7)) multiplexer_37 (
    .sel(comparator_2_eq), .in_0(multiplexer_35_out), .in_1(7'b1000001), .out(multiplexer_37_out));
  Multiplexer #(.Selector_Bits(3), .Bits(7)) multiplexer_38 (
    .sel(multiplexer_3_out), .in_0(multiplexer_36_out), .in_1(7'b1010010), .in_2(7'b1001100),
    .in_3(multiplexer_39_out), .in_4(multiplexer_18_out), .in_5(multiplexer_24_out), .in_6(7'b1010111),
    .in_7(7'b1010111), .out(multiplexer_38_out));
  Multiplexer #(.Bits(7)) multiplexer_39 (
    .sel(and_11_out), .in_0(multiplexer_37_out), .in_1(7'b1001100), .out(multiplexer_39_out));
  Multiplexer #(.Bits(7)) multiplexer_40 (
    .sel(comparator_6_eq), .in_0(7'b1000001), .in_1(7'b1001101), .out(multiplexer_40_out));
  ROM #(.AddrBits(7), .Bits(16)) ASCII_6 (.A(multiplexer_38_out), .sel(1'b1), .D(D6));
  Multiplexer #(.Bits(7)) multiplexer_41 (.sel(ALUControl[3]), .in_0(multiplexer_40_out), .in_1(7'b1001100), .out(y0));
  Comparator comparator_6 (.a(funct7[0]), .b(1'b1), .eq(comparator_6_eq));  // open: gt, lt
  Multiplexer #(.Bits(7)) multiplexer_42 (
    .sel(comparator_6_eq), .in_0(7'b1001110), .in_1(7'b1010101), .out(multiplexer_42_out));
  Multiplexer #(.Bits(7)) multiplexer_43 (.sel(ALUControl[3]), .in_0(multiplexer_42_out), .in_1(7'b1010100), .out(y1));
  Multiplexer #(.Bits(7)) multiplexer_44 (
    .sel(comparator_6_eq), .in_0(7'b1000100), .in_1(7'b1001100), .out(multiplexer_44_out));
  Multiplexer #(.Bits(7)) multiplexer_45 (.sel(ALUControl[3]), .in_0(multiplexer_44_out), .in_1(7'b1010101), .out(y2));

  assign P1 = 1'b0;
  assign P2 = 1'b0;
  assign P3 = 1'b0;
  assign P4 = 1'b0;
  assign P5 = 1'b0;
  assign P6 = 1'b0;

  // Other names for the same wires on the sheet: LUI_AUIPC_sel[1:0] = {AUIPC, LUI}

  // Notes on the sheet:
  //   0000011
  //   0100011
  //   1100011
  //   0010011
  //   0110011
  //   1101111
  //   1100111
  //   0110111
  //   0010111
  //   contents of ASCII (hex, n*v repeats v):
  //   90ff,c,377,33f,38c,3bb,3fb,f,3ff,3bf,3cf,4a3f,f3,483f,3f3,1c3
  //   ,17*0,4800,4*0,2d79,4*0,4b00,0,300,0,0,90ff,c,377,33f,38c,3bb
  //   ,3fb,f,3ff,3bf,0,0,3000,0,8400,0,0,3cf,4a3f,f3,483f,3f3,1c3,2fb
  //   ,3cc,4833,7c,31c0,f0,14cc,24cc,ff,3c7,20ff,23c7,3bb,4803,fc,90c0
  //   ,a0cc,b400,5400,9033,0,0,0,a000
  //   contents of ASCII_2 (hex, n*v repeats v):
  //   90ff,c,377,33f,38c,3bb,3fb,f,3ff,3bf,3cf,4a3f,f3,483f,3f3,1c3
  //   ,17*0,4800,4*0,2d79,4*0,4b00,0,300,0,0,90ff,c,377,33f,38c,3bb
  //   ,3fb,f,3ff,3bf,0,0,3000,0,8400,0,0,3cf,4a3f,f3,483f,3f3,1c3,2fb
  //   ,3cc,4833,7c,31c0,f0,14cc,24cc,ff,3c7,20ff,23c7,3bb,4803,fc,90c0
  //   ,a0cc,b400,5400,9033,0,0,0,a000
  //   contents of ASCII_3 (hex, n*v repeats v):
  //   90ff,c,377,33f,38c,3bb,3fb,f,3ff,3bf,3cf,4a3f,f3,483f,3f3,1c3
  //   ,17*0,4800,4*0,2d79,4*0,4b00,0,300,0,0,90ff,c,377,33f,38c,3bb
  //   ,3fb,f,3ff,3bf,0,0,3000,0,8400,0,0,3cf,4a3f,f3,483f,3f3,1c3,2fb
  //   ,3cc,4833,7c,31c0,f0,14cc,24cc,ff,3c7,20ff,23c7,3bb,4803,fc,90c0
  //   ,a0cc,b400,5400,9033,0,0,0,a000
  //   contents of ASCII_4 (hex, n*v repeats v):
  //   90ff,c,377,33f,38c,3bb,3fb,f,3ff,3bf,3cf,4a3f,f3,483f,3f3,1c3
  //   ,17*0,4800,4*0,2d79,4*0,4b00,0,300,0,0,90ff,c,377,33f,38c,3bb
  //   ,3fb,f,3ff,3bf,0,0,3000,0,8400,0,0,3cf,4a3f,f3,483f,3f3,1c3,2fb
  //   ,3cc,4833,7c,31c0,f0,14cc,24cc,ff,3c7,20ff,23c7,3bb,4803,fc,90c0
  //   ,a0cc,b400,5400,9033,0,0,0,a000
  //   contents of ASCII_5 (hex, n*v repeats v):
  //   90ff,c,377,33f,38c,3bb,3fb,f,3ff,3bf,3cf,4a3f,f3,483f,3f3,1c3
  //   ,17*0,4800,4*0,2d79,4*0,4b00,0,300,0,0,90ff,c,377,33f,38c,3bb
  //   ,3fb,f,3ff,3bf,0,0,3000,0,8400,0,0,3cf,4a3f,f3,483f,3f3,1c3,2fb
  //   ,3cc,4833,7c,31c0,f0,14cc,24cc,ff,3c7,20ff,23c7,3bb,4803,fc,90c0
  //   ,a0cc,b400,5400,9033,0,0,0,a000
  //   contents of ASCII_6 (hex, n*v repeats v):
  //   90ff,c,377,33f,38c,3bb,3fb,f,3ff,3bf,3cf,4a3f,f3,483f,3f3,1c3
  //   ,17*0,4800,4*0,2d79,4*0,4b00,0,300,0,0,90ff,c,377,33f,38c,3bb
  //   ,3fb,f,3ff,3bf,0,0,3000,0,8400,0,0,3cf,4a3f,f3,483f,3f3,1c3,2fb
  //   ,3cc,4833,7c,31c0,f0,14cc,24cc,ff,3c7,20ff,23c7,3bb,4803,fc,90c0
  //   ,a0cc,b400,5400,9033,0,0,0,a000
endmodule
